// Logisim project easyone.circ as structural Verilog: 1 circuit, main circuit main
module main (
  input  [3:0] A,
  input  [3:0] B
);

  wire comparator_1_eq, comparator_1_gt, comparator_1_lt;

  Comparator #(.width(4), .mode("unsigned")) comparator_1 (
    .a(A), .b(B), .gt(comparator_1_gt), .eq(comparator_1_eq), .lt(comparator_1_lt));
  LED led_1 (.in(comparator_1_gt));
  LED led_2 (.in(comparator_1_eq));
  LED led_3 (.in(comparator_1_lt));
endmodule
